// Logisim project control-logic.circ as structural Verilog: 1 circuit, main circuit control_logic
module control_logic (
  input  [31:0] inst,
  input  BrEq,
  input  BrLt,
  output PCSel,
  output RegWEn,
  output [2:0] ImmSel,
  output BrUn,
  output ASel,
  output BSel,
  output [3:0] ALUSel,
  output MemRW,
  output [1:0] WBSel,
  output CSRSel,
  output CSRWen
);

  wire demultiplexer_1_out0, demultiplexer_1_out1, demultiplexer_2_out0, demultiplexer_2_out1,
       demultiplexer_3_out0, demultiplexer_3_out1, demultiplexer_4_out1, demultiplexer_5_out1,
       priority_encoder_2_gs, ROM_I2, ROM_UJ, TYPE_CSR, TYPE_I, TYPE_R, TYPE_S, TYPE_SB, TYPE_U;
  wire [1:0] bit_extender_4_out, bit_extender_5_out, ROM_CSR, ROM_U, undriven, undriven_6;
  wire [2:0] bit_extender_6_out, priority_encoder_2_out, ROM_S, undriven_3;
  wire [4:0] priority_encoder_1_out;
  wire [5:0] adder_1_out, bit_extender_3_out, ROM_IN, ROM_SB, undriven_4;
  wire [10:0] bit_extender_2_out, ROM_I, undriven_2;
  wire [11:0] bit_extender_1_out, ROM_R, undriven_5;
  wire [15:0] rom_1_data;

  Demultiplexer #(.enable("false")) demultiplexer_1 (
    .out0(demultiplexer_1_out0), .out1(demultiplexer_1_out1), .in(1'b1), .sel(inst[14]));
  Demultiplexer #(.enable("false")) demultiplexer_2 (
    .out0(demultiplexer_2_out0), .out1(demultiplexer_2_out1), .in(demultiplexer_1_out1), .sel(inst[13]));
  Demultiplexer #(.enable("false")) demultiplexer_3 (
    .out0(demultiplexer_3_out0), .out1(demultiplexer_3_out1), .in(demultiplexer_1_out0), .sel(inst[12]));
  Demultiplexer #(.enable("false")) demultiplexer_4 (
    .out0(undriven_5[3]), .out1(demultiplexer_4_out1), .in(demultiplexer_3_out1), .sel(inst[25]));
  Demultiplexer #(.enable("false")) demultiplexer_5 (
    .out0(undriven_5[7]), .out1(demultiplexer_5_out1), .in(demultiplexer_2_out0), .sel(inst[12]));
  Demultiplexer #(.enable("false")) demultiplexer_6 (
    .out0(undriven_5[10]), .out1(undriven_5[11]), .in(demultiplexer_2_out1), .sel(inst[12]));
  Demultiplexer #(.enable("false")) demultiplexer_7 (
    .out1(undriven_5[6]), .in(demultiplexer_3_out0), .sel(inst[13]));  // open: out0
  Demultiplexer #(.enable("false")) demultiplexer_8 (
    .out0(undriven_5[4]), .out1(undriven_5[5]), .in(demultiplexer_4_out1), .sel(inst[13]));
  ROM #(.addrWidth(6), .dataWidth(16)) rom_1 (.addr(ROM_IN), .data(rom_1_data));
  Demultiplexer #(.enable("false")) demultiplexer_9 (
    .out0(undriven_5[8]), .out1(undriven_5[9]), .in(demultiplexer_5_out1), .sel(inst[30]));
  assign bit_extender_1_out = {{11{TYPE_R}}, TYPE_R};  // Bit_Extender bit_extender_1
  assign bit_extender_2_out = {{10{TYPE_I}}, TYPE_I};  // Bit_Extender bit_extender_2
  assign bit_extender_3_out = {{5{TYPE_SB}}, TYPE_SB};  // Bit_Extender bit_extender_3
  assign bit_extender_4_out = {{1{TYPE_U}}, TYPE_U};  // Bit_Extender bit_extender_4
  assign bit_extender_5_out = {{1{TYPE_CSR}}, TYPE_CSR};  // Bit_Extender bit_extender_5
  assign ROM_R = bit_extender_1_out & undriven_5;  // AND_Gate and_1, 12 bits wide
  assign bit_extender_6_out = {{2{TYPE_S}}, TYPE_S};  // Bit_Extender bit_extender_6
  assign ROM_SB = bit_extender_3_out & undriven_4;  // AND_Gate and_2, 6 bits wide
  assign ROM_U = bit_extender_4_out & undriven;  // AND_Gate and_3, 2 bits wide
  assign ROM_I = bit_extender_2_out & undriven_2;  // AND_Gate and_4, 11 bits wide
  assign ROM_S = bit_extender_6_out & undriven_3;  // AND_Gate and_5, 3 bits wide
  assign ROM_CSR = bit_extender_5_out & undriven_6;  // AND_Gate and_6, 2 bits wide
  Priority_Encoder #(.select(5)) priority_encoder_1 (
    .in0(ROM_R[0]), .in1(ROM_R[1]), .in2(ROM_R[2]), .in3(ROM_R[3]), .in4(ROM_R[4]), .in5(ROM_R[5]),
    .in6(ROM_R[6]), .in7(ROM_R[7]), .in8(ROM_R[8]), .in9(ROM_R[9]), .in10(ROM_R[10]), .in11(ROM_R[11]),
    .in12(ROM_I[0]), .in13(ROM_I[1]), .in14(ROM_I[2]), .in15(ROM_I[3]), .in16(ROM_I[4]), .in17(ROM_I[5]),
    .in18(ROM_I[6]), .in19(ROM_I[7]), .in20(ROM_I[8]), .in21(ROM_I[9]), .in22(ROM_I[10]), .in23(ROM_S[0]),
    .in24(ROM_S[1]), .in25(ROM_S[2]), .in26(ROM_SB[0]), .in27(ROM_SB[1]), .in28(ROM_SB[2]), .in29(ROM_SB[3]),
    .in30(ROM_SB[4]), .in31(ROM_SB[5]), .out(priority_encoder_1_out));  // open: gs, en_out, en_in
  Priority_Encoder priority_encoder_2 (
    .in0(ROM_U[0]), .in1(ROM_U[1]), .in2(ROM_UJ), .in3(ROM_I2), .in4(ROM_CSR[0]), .in5(ROM_CSR[1]),
    .out(priority_encoder_2_out), .gs(priority_encoder_2_gs));  // open: in6, in7, en_in, en_out
  Adder #(.width(6)) adder_1 (
    .a({3'b000, priority_encoder_2_out}), .b(6'b100000), .out(adder_1_out));  // open: cin, cout
  Multiplexer #(.enable("false"), .width(6)) multiplexer_1 (
    .in0({1'b0, priority_encoder_1_out}), .in1(adder_1_out), .out(ROM_IN), .sel(priority_encoder_2_gs));
  and and_7 (TYPE_R, ~inst[6], inst[5], inst[4], ~inst[3], ~inst[2], inst[1], inst[0]);  // AND_Gate
  and and_8 (TYPE_I, ~inst[6], ~inst[5], 1'b1, ~inst[3], ~inst[2], inst[1], inst[0]);  // AND_Gate
  and and_9 (TYPE_S, ~inst[6], inst[5], ~inst[4], ~inst[3], ~inst[2], inst[1], inst[0]);  // AND_Gate
  and and_10 (TYPE_SB, inst[6], inst[5], ~inst[4], ~inst[3], ~inst[2], inst[1], inst[0]);  // AND_Gate
  and and_11 (TYPE_U, ~inst[6], inst[5], 1'b1, ~inst[3], inst[2], inst[1], inst[0]);  // AND_Gate
  and and_12 (ROM_UJ, inst[6], inst[5], ~inst[4], inst[3], inst[2], inst[1], inst[0]);  // AND_Gate
  and and_13 (ROM_I2, inst[6], inst[5], ~inst[4], ~inst[3], inst[2], inst[1], inst[0]);  // AND_Gate
  and and_14 (TYPE_CSR, inst[6], inst[5], inst[4], ~inst[3], ~inst[2], inst[1], inst[0]);  // AND_Gate

  // Other names for the same wires on the sheet: OP7 = inst[0]; OP6 = inst[1]; OP5 = inst[2]; OP4 = inst[3];
  //   OP3 = inst[4]; OP2 = inst[5]; OP1 = inst[6]; f3_3 = inst[12]; f3_2 = inst[13]; f3_1 = inst[14]; f7_7 = inst[25];
  //   f7_6 = inst[26]; f7_5 = inst[27]; f7_4 = inst[28]; f7_3 = inst[29]; f7_2 = inst[30]; f7_1 = inst[31];
  //   TYPE_I2 = ROM_I2; TYPE_UJ = ROM_UJ

  // Notes on the sheet:
  //   INPUTS to your circuit
  //   Connect ROM Input here ->
  //   contents of rom_1 (hex, n*v repeats v):
  //   12*0 4*9204 9224 9244 9284 92a4 93a4 92c4 92e4
  //   ROM FOR CONTROL LOGIC
  //   DON'T CHANGE THE LOCATIONS OF THE INPUTS AND OUTPUTS!
  //   OUTPUT from your circuit
  //   CLOSE
  //   WIRE
  //   TO
  //   USE
  //   ROM
  //   Reminder: Use combinational logic for PCSel
endmodule
