// Logisim project cpu.circ as structural Verilog: 1 circuit, main circuit cpu
module cpu (
  input  clk,
  input  [31:0] INSTRUCTION,
  input  [31:0] MEM_READ_DATA,
  output [31:0] MEM_WRITE_ADDRESS,
  output [31:0] PROGRAM_COUNTER,
  output [31:0] ra,
  output [31:0] sp,
  output [31:0] t0,
  output [31:0] t1,
  output [31:0] t2,
  output [31:0] s0,
  output [31:0] s1,
  output [31:0] a0,
  output [31:0] tohost,
  output [3:0] MEM_WRITE_ENABLE,
  output [31:0] MEM_WRITE_DATA
);

  wire ASel, BrEq, BrLt, BrUn, BSel, MemRW, PCSel, RegWEn;
  wire [1:0] WBSel;
  wire [2:0] ImmSel;
  wire [3:0] ALUSel, multiplexer_8_out;
  wire [31:0] bit_extender_1_out, bit_extender_2_out, bit_extender_3_out, bit_extender_4_out,
       bit_extender_5_out, bit_extender_6_out, imm, mem_to_reg, multiplexer_1_out, multiplexer_2_out,
       multiplexer_3_out, multiplexer_4_out, multiplexer_5_out, PC4, RD1, wb;

  Adder #(.width(32)) adder_1 (.a(PROGRAM_COUNTER), .b(32'h4), .out(PC4));  // open: cin, cout
  Register #(.width(32)) PC (.D(multiplexer_1_out), .clk(clk), .Q(PROGRAM_COUNTER));  // open: en, clr
  Multiplexer #(.enable("false"), .width(32)) multiplexer_1 (
    .in0(PC4), .in1(MEM_WRITE_ADDRESS), .out(multiplexer_1_out), .sel(PCSel));
  control_logic control_logic_1 (
    .PCSel(PCSel), .RegWEn(RegWEn), .ImmSel(ImmSel), .BrUn(BrUn), .ASel(ASel), .BSel(BSel), .ALUSel(ALUSel),
    .MemRW(MemRW), .WBSel(WBSel), .inst(INSTRUCTION), .BrEq(BrEq), .BrLt(BrLt));  // open: CSRWen, CSRSel
  imm_gen imm_gen_1 (.inst(INSTRUCTION), .ImmSel(ImmSel), .imm(imm));
  regfile regfile_1 (
    .rs1(INSTRUCTION[19:15]), .rs2(INSTRUCTION[24:20]), .rd(INSTRUCTION[11:7]), .Write_Data(wb),
    .RegWEn(RegWEn), .clk(clk), .ra(ra), .sp(sp), .t0(t0), .t1(t1), .t2(t2), .s0(s0), .s1(s1), .a0(a0),
    .Read_Data_1(RD1), .Read_Data_2(MEM_WRITE_DATA));
  branch_comp branch_comp_1 (.rs1(RD1), .rs2(MEM_WRITE_DATA), .BrUn(BrUn), .BrEq(BrEq), .BrLt(BrLt));
  Multiplexer #(.enable("false"), .width(32)) multiplexer_2 (
    .in0(RD1), .in1(PROGRAM_COUNTER), .out(multiplexer_2_out), .sel(ASel));
  Multiplexer #(.enable("false"), .width(32)) multiplexer_3 (
    .in0(MEM_WRITE_DATA), .in1(imm), .out(multiplexer_3_out), .sel(BSel));
  alu alu_1 (.Result(MEM_WRITE_ADDRESS), .A(multiplexer_2_out), .B(multiplexer_3_out), .ALUSel(ALUSel));
  // csr csr_1: pin names not known; wires that end beside it: tohost
  assign bit_extender_1_out = {{24{MEM_READ_DATA[7]}}, MEM_READ_DATA[7:0]};  // Bit_Extender bit_extender_1
  assign bit_extender_2_out = {{24{MEM_READ_DATA[15]}}, MEM_READ_DATA[15:8]};  // Bit_Extender bit_extender_2
  assign bit_extender_3_out = {{24{MEM_READ_DATA[23]}}, MEM_READ_DATA[23:16]};  // Bit_Extender bit_extender_3
  assign bit_extender_4_out = {{24{MEM_READ_DATA[31]}}, MEM_READ_DATA[31:24]};  // Bit_Extender bit_extender_4
  assign bit_extender_5_out = {{16{MEM_READ_DATA[15]}}, MEM_READ_DATA[15:0]};  // Bit_Extender bit_extender_5
  assign bit_extender_6_out = {{16{MEM_READ_DATA[31]}}, MEM_READ_DATA[31:16]};  // Bit_Extender bit_extender_6
  Multiplexer #(.enable("false"), .select(2), .width(32)) multiplexer_4 (
    .in0(bit_extender_1_out), .in1(bit_extender_2_out), .in2(bit_extender_3_out), .in3(bit_extender_4_out),
    .out(multiplexer_4_out), .sel(imm[1:0]));
  Multiplexer #(.enable("false"), .select(2), .width(32)) multiplexer_5 (
    .in0(bit_extender_5_out), .in2(bit_extender_6_out), .out(multiplexer_5_out), .sel(imm[1:0]));  // open: in1, in3
  Multiplexer #(.enable("false"), .select(2), .width(32)) multiplexer_6 (
    .in0(multiplexer_4_out), .in1(multiplexer_5_out), .in2(MEM_READ_DATA), .out(mem_to_reg),
    .sel(INSTRUCTION[13:12]));  // open: in3
  Multiplexer #(.enable("false"), .select(2), .width(32)) multiplexer_7 (
    .in0(mem_to_reg), .in1(MEM_WRITE_ADDRESS), .in2(PC4), .out(wb), .sel(WBSel));  // open: in3
  Multiplexer #(.enable("false"), .select(4), .width(4)) multiplexer_8 (
    .in0(4'b0000), .in1(4'b0010), .in2(4'b0100), .in3(4'b1000), .in4(4'b0011), .in6(4'b1100), .in8(4'b1111),
    .out(multiplexer_8_out), .sel({INSTRUCTION[13:12], imm[1:0]}));  // open: in5, in7, in9, in10, in11, in12, in13, in14, in15
  Multiplexer #(.enable("false"), .width(4)) multiplexer_9 (
    .in0(4'b0000), .in1(multiplexer_8_out), .out(MEM_WRITE_ENABLE), .sel(MemRW));

  // Other names for the same wires on the sheet: last2digits[1:0] = imm[1:0]; f3_3 = INSTRUCTION[12];
  //   f3_2 = INSTRUCTION[13]; alu_result[31:0] = MEM_WRITE_ADDRESS; rd[4:0] = INSTRUCTION[11:7];
  //   f3_1 = INSTRUCTION[14]; rs1[4:0] = INSTRUCTION[19:15]; rs2[4:0] = INSTRUCTION[24:20]; f7_7 = INSTRUCTION[25];
  //   f7_6 = INSTRUCTION[26]; f7_5 = INSTRUCTION[27]; f7_4 = INSTRUCTION[28]; f7_3 = INSTRUCTION[29];
  //   f7_2 = INSTRUCTION[30]; f7_1 = INSTRUCTION[31]; PC[31:0] = PROGRAM_COUNTER; RD2[31:0] = MEM_WRITE_DATA

  // Notes on the sheet:
  //   Output to IMEM
  //   IMEM (do **NOT** move this)
  //   Inputs from IMEM
  //   It is OK to move the PC, RegFile, ALU, MEM, Branch Comp, Imm Gen, and Control Logic to wherever is most convenient for you when constructing your CPU, and to delete this text
  //   Inputs/Outputs for testing. Do **NOT** move these.
  //   Outputs To DMEM
  //   DMEM (do **NOT** move this)
  //   Inputs From DMEM
endmodule
